// Logisim project cpu.circ as structural Verilog: 5 circuits, main circuit main
module main (
  input  cleardata,
  output [15:0] out_2,
  output [2:0] writereg,
  output [2:0] data22,
  output [15:0] out_5,
  output [2:0] data11,
  output [15:0] out_7,
  output [15:0] out_8,
  output [4:0] out_9,
  output [15:0] writedata,
  output [10:0] out_11
);

  wire alu_1_is_ble, clock_1_out, cu_1_alusrc, cu_1_branch, cu_1_call, cu_1_halt, cu_1_memread,
       cu_1_memtoreg, cu_1_memwrite, cu_1_reboot, cu_1_regdst, cu_1_regwrite, cu_1_rtn, cu_1_typei;
  wire [2:0] multiplexer_1_out;
  wire [3:0] cu_1_aluop;
  wire [15:0] bit_extender_1_out, multiplexer_3_out, ram_2_dout, registerfile_1_data1, registerfile_1_data2;

  Clock clock_1 (.out(clock_1_out));
  PC pc_1 (
    .Value_of_PC_14cdde46(out_5), .Halt(cu_1_halt), .Call(cu_1_call), .Branch(cu_1_branch), .Rtn(cu_1_rtn),
    .Reboot(cu_1_reboot), .Clear(cleardata), .CLK(clock_1_out), .x(bit_extender_1_out), .is_ble(alu_1_is_ble));
  RAM #(.addrWidth(16), .dataWidth(16)) ram_1 (
    .addr(out_5), .we(1'b0), .oe(1'b1), .clk(clock_1_out), .dout({out_8[15:11], data11, out_8[7:0]}));  // open: din
  assign bit_extender_1_out = {{11{out_8[7]}}, out_8[7:3]};  // Bit_Extender bit_extender_1
  Multiplexer #(.enable("false"), .width(3)) multiplexer_1 (
    .in0(out_8[2:0]), .in1(out_8[7:5]), .out(multiplexer_1_out), .sel(cu_1_regdst));
  Multiplexer #(.enable("false"), .width(3)) multiplexer_2 (
    .in0(multiplexer_1_out), .in1(data11), .out(data22), .sel(cu_1_typei));
  registerFile registerfile_1 (
    .data1(registerfile_1_data1), .data2(registerfile_1_data2), .CLK(clock_1_out), .reset(cleardata),
    .register2(data22), .register1(data11), .halt(cu_1_halt), .registerwriter(out_8[2:0]),
    .write(cu_1_regwrite), .Writer(writedata));
  CU cu_1 (
    .MemToReg(cu_1_memtoreg), .MemRead(cu_1_memread), .MemWrite(cu_1_memwrite), .call(cu_1_call),
    .rtn(cu_1_rtn), .reboot(cu_1_reboot), .halt(cu_1_halt), .typeI(cu_1_typei), .RegWrite(cu_1_regwrite),
    .branch(cu_1_branch), .ALUsrc(cu_1_alusrc), .RegDst(cu_1_regdst), .ALUOp(cu_1_aluop),
    .opcode(out_8[15:11]));  // open: isALU
  Multiplexer #(.enable("false"), .width(16)) multiplexer_3 (
    .in0(registerfile_1_data1), .in1(bit_extender_1_out), .out(multiplexer_3_out), .sel(cu_1_alusrc));
  ALU alu_1 (
    .AluRes(out_2), .is_ble(alu_1_is_ble), .in_3(cu_1_aluop), .Data1(multiplexer_3_out),
    .Data2(registerfile_1_data2));
  RAM #(.addrWidth(16), .clearpin("true"), .dataWidth(16)) ram_2 (
    .addr(registerfile_1_data2), .we(cu_1_memwrite), .oe(cu_1_memread), .clk(clock_1_out), .din(out_2),
    .dout(ram_2_dout), .clr(cleardata));
  Multiplexer #(.enable("false"), .width(16)) multiplexer_4 (
    .in0(out_2), .in1(ram_2_dout), .out(writedata), .sel(cu_1_memtoreg));

  assign out_7 = out_2;
  assign out_8[10:8] = data11;
  assign out_9 = out_8[7:3];
  assign out_11 = {data11, out_8[7:0]};
  assign writereg = out_8[2:0];
endmodule

module registerFile (
  input  [15:0] Writer,
  input  [2:0] registerwriter,
  input  write,
  input  [2:0] register2,
  input  CLK,
  input  reset,
  input  [2:0] register1,
  input  halt,
  output [15:0] data1,
  output [15:0] data2
);

  wire and_1_out, and_2_out, and_3_out, and_4_out, and_5_out, and_6_out, and_7_out, and_8_out, and_9_out,
       decoder_1_out0, decoder_1_out1, decoder_1_out2, decoder_1_out3, decoder_1_out4, decoder_1_out5,
       decoder_1_out6, decoder_1_out7, not_1_out;
  wire [15:0] register_1_q, register_2_q, register_3_q, register_4_q, register_5_q, register_6_q,
       register_7_q, register_8_q;

  Decoder #(.enable("false"), .select(3)) decoder_1 (
    .out0(decoder_1_out0), .out1(decoder_1_out1), .out2(decoder_1_out2), .out3(decoder_1_out3),
    .out4(decoder_1_out4), .out5(decoder_1_out5), .out6(decoder_1_out6), .out7(decoder_1_out7),
    .sel(registerwriter));
  not not_1 (not_1_out, halt);
  and and_1 (and_1_out, write, not_1_out);
  and and_2 (and_2_out, and_1_out, decoder_1_out0);
  and and_3 (and_3_out, and_1_out, decoder_1_out1);
  and and_4 (and_4_out, and_1_out, decoder_1_out2);
  and and_5 (and_5_out, and_1_out, decoder_1_out3);
  and and_6 (and_6_out, and_1_out, decoder_1_out4);
  and and_7 (and_7_out, and_1_out, decoder_1_out5);
  and and_8 (and_8_out, and_1_out, decoder_1_out6);
  and and_9 (and_9_out, and_1_out, decoder_1_out7);
  Register #(.width(16)) register_1 (.D(Writer), .en(and_2_out), .clk(CLK), .Q(register_1_q), .clr(reset));
  Register #(.width(16)) register_2 (.D(Writer), .en(and_3_out), .clk(CLK), .Q(register_2_q), .clr(reset));
  Register #(.width(16)) register_3 (.D(Writer), .en(and_4_out), .clk(CLK), .Q(register_3_q), .clr(reset));
  Register #(.width(16)) register_4 (.D(Writer), .en(and_5_out), .clk(CLK), .Q(register_4_q), .clr(reset));
  Register #(.width(16)) register_5 (.D(Writer), .en(and_6_out), .clk(CLK), .Q(register_5_q), .clr(reset));
  Register #(.width(16)) register_6 (.D(Writer), .en(and_7_out), .clk(CLK), .Q(register_6_q), .clr(reset));
  Register #(.width(16)) register_7 (.D(Writer), .en(and_8_out), .clk(CLK), .Q(register_7_q), .clr(reset));
  Register #(.width(16)) register_8 (.D(Writer), .en(and_9_out), .clk(CLK), .Q(register_8_q), .clr(reset));
  Multiplexer #(.enable("false"), .select(3), .width(16)) multiplexer_1 (
    .in0(register_1_q), .in1(register_2_q), .in2(register_3_q), .in3(register_4_q), .in4(register_5_q),
    .in5(register_6_q), .in6(register_7_q), .in7(register_8_q), .out(data1), .sel(register1));
  Multiplexer #(.enable("false"), .select(3), .width(16)) multiplexer_2 (
    .in0(register_1_q), .in1(register_2_q), .in2(register_3_q), .in3(register_4_q), .in4(register_5_q),
    .in5(register_6_q), .in6(register_7_q), .in7(register_8_q), .out(data2), .sel(register2));
endmodule

module PC (
  input  Halt,
  input  Call,
  input  Rtn,
  input  Reboot,
  input  [15:0] x,
  input  is_ble,
  input  Branch,
  input  Clear,
  input  CLK,
  output [15:0] Value_of_PC_14cdde46
);

  wire and_1_out, not_1_out, or_1_out;
  wire [15:0] adder_1_out, adder_2_out, adder_3_out, multiplexer_1_out, multiplexer_2_out, multiplexer_3_out,
       multiplexer_4_out, multiplexer_5_out, multiplexer_6_out, RA_q, register_1_q, subtractor_1_out,
       subtractor_2_out;

  not not_1 (not_1_out, Halt);
  Adder #(.width(16)) adder_1 (.a(x), .b(multiplexer_3_out), .out(adder_1_out));  // open: cin, cout
  and and_1 (and_1_out, not_1_out, Call);
  Subtractor #(.width(16)) subtractor_1 (.a(adder_1_out), .b(16'h1), .out(subtractor_1_out));  // open: bin, bout
  or or_1 (or_1_out, is_ble, Branch);
  Multiplexer #(.enable("false"), .width(16)) multiplexer_1 (
    .in0(multiplexer_5_out), .in1({16{1'b0}}), .out(multiplexer_1_out), .sel(Reboot));
  Register #(.width(16)) register_1 (.D(multiplexer_2_out), .en(not_1_out), .clk(CLK), .Q(register_1_q), .clr(Clear));
  Multiplexer #(.enable("false"), .width(16)) multiplexer_2 (
    .in0(multiplexer_3_out), .in1(subtractor_1_out), .out(multiplexer_2_out), .sel(or_1_out));
  Multiplexer #(.enable("false"), .width(16)) multiplexer_3 (
    .in0(multiplexer_1_out), .in1(RA_q), .out(multiplexer_3_out), .sel(Rtn));
  Register #(.width(16)) RA (.D(register_1_q), .en(and_1_out), .clk(CLK), .Q(RA_q), .clr(Clear));
  Adder #(.width(16)) adder_2 (.a(16'h1), .b(register_1_q), .out(adder_2_out));  // open: cin, cout
  Adder #(.width(16)) adder_3 (.a(register_1_q), .b(x), .out(adder_3_out));  // open: cin, cout
  Multiplexer #(.enable("false"), .width(16)) multiplexer_4 (
    .in0(register_1_q), .in1(subtractor_2_out), .out(multiplexer_4_out), .sel(or_1_out));
  Subtractor #(.width(16)) subtractor_2 (.a(adder_3_out), .b(16'h1), .out(subtractor_2_out));  // open: bin, bout
  Multiplexer #(.enable("false"), .width(16)) multiplexer_5 (
    .in0(adder_2_out), .in1(register_1_q), .out(multiplexer_5_out), .sel(or_1_out));
  Multiplexer #(.enable("false"), .width(16)) multiplexer_6 (
    .in0(multiplexer_4_out), .in1(RA_q), .out(multiplexer_6_out), .sel(Rtn));
  Multiplexer #(.enable("false"), .width(16)) multiplexer_7 (
    .in0(multiplexer_6_out), .in1({16{1'b0}}), .out(Value_of_PC_14cdde46), .sel(Reboot));
endmodule

module ALU (
  input  [15:0] Data1,
  input  [15:0] Data2,
  input  [3:0] in_3,
  output [15:0] AluRes,
  output is_ble
);

  wire comparator_1_lt, comparator_2_eq, comparator_2_gt, comparator_3_eq, or_2_out;
  wire [15:0] adder_1_out, adder_2_out, and_1_out, multiplexer_1_out, negator_1_out, or_1_out, shifter_1_out,
       shifter_2_out;

  Adder #(.width(16)) adder_1 (.a(Data1), .b(Data2), .out(adder_1_out));  // open: cin, cout
  assign and_1_out = Data1 & Data2;  // AND_Gate and_1, 16 bits wide
  assign or_1_out = Data1 | Data2;  // OR_Gate or_1, 16 bits wide
  Comparator #(.width(16)) comparator_1 (.a(Data1), .b(Data2), .lt(comparator_1_lt));  // open: gt, eq
  Shifter #(.width(16)) shifter_1 (.in(Data1), .\dist (Data2[3:0]), .out(shifter_1_out));
  Shifter #(.shift("lr"), .width(16)) shifter_2 (.in(Data1), .\dist (Data2[3:0]), .out(shifter_2_out));
  Comparator #(.width(16)) comparator_2 (.a(Data1), .b(Data2), .gt(comparator_2_gt), .eq(comparator_2_eq));  // open: lt
  Adder #(.width(16)) adder_2 (.a(Data2), .b({16{1'b0}}), .out(adder_2_out));  // open: cin, cout
  Negator #(.width(16)) negator_1 (.in(Data1), .out(negator_1_out));
  Multiplexer #(.enable("false"), .width(16)) multiplexer_1 (
    .in0({16{1'b0}}), .in1(16'h1), .out(multiplexer_1_out), .sel(comparator_1_lt));
  or or_2 (or_2_out, comparator_2_gt, comparator_2_eq);
  Multiplexer multiplexer_2 (.in0(1'b0), .in1(1'b1), .out(is_ble), .sel(or_2_out), .en(comparator_3_eq));
  Multiplexer #(.enable("false"), .select(4), .width(16)) multiplexer_3 (
    .in0(adder_1_out), .in1(and_1_out), .in2(or_1_out), .in3(multiplexer_1_out), .in4(shifter_1_out),
    .in5(shifter_2_out), .in6(Data1), .in10(Data1), .in12(adder_2_out), .in13(Data1), .in15(negator_1_out),
    .out(AluRes), .sel(in_3));  // open: in7, in8, in9, in11, in14
  Comparator #(.width(4)) comparator_3 (.a(in_3), .b(4'b1000), .eq(comparator_3_eq));  // open: gt, lt
endmodule

module CU (
  input  [4:0] opcode,
  output [3:0] ALUOp,
  output isALU,
  output RegDst,
  output ALUsrc,
  output MemToReg,
  output RegWrite,
  output MemRead,
  output MemWrite,
  output branch,
  output call,
  output rtn,
  output reboot,
  output halt,
  output typeI
);

  wire demultiplexer_1_out0, demultiplexer_1_out1, demultiplexer_1_out2, demultiplexer_1_out3,
       demultiplexer_1_out4, demultiplexer_1_out7, demultiplexer_1_out8, demultiplexer_1_out9,
       demultiplexer_1_out10, demultiplexer_1_out11, demultiplexer_1_out12, demultiplexer_1_out13,
       demultiplexer_1_out14, demultiplexer_1_out15, or_1_out, or_2_out, or_3_out, or_4_out, or_8_out,
       or_9_out, or_11_out;

  Demultiplexer #(.enable("false"), .select(5)) demultiplexer_1 (
    .out0(demultiplexer_1_out0), .out1(demultiplexer_1_out1), .out2(demultiplexer_1_out2),
    .out3(demultiplexer_1_out3), .out4(demultiplexer_1_out4), .out5(MemRead), .out6(MemWrite),
    .out7(demultiplexer_1_out7), .out8(demultiplexer_1_out8), .out9(demultiplexer_1_out9),
    .out10(demultiplexer_1_out10), .out11(demultiplexer_1_out11), .out12(demultiplexer_1_out12),
    .out13(demultiplexer_1_out13), .out14(demultiplexer_1_out14), .out15(demultiplexer_1_out15),
    .out16(call), .out17(rtn), .out18(reboot), .out19(halt), .in(1'b1), .sel(opcode));  // open: out20, out21, out22, out23, out24, out25, out26, out27, out28, out29, out30, out31
  or or_1 (or_1_out, demultiplexer_1_out11, demultiplexer_1_out15);
  or or_2 (or_2_out, MemWrite, rtn);
  or or_3 (or_3_out, demultiplexer_1_out8, demultiplexer_1_out1);
  or or_4 (or_4_out, demultiplexer_1_out3, demultiplexer_1_out10);
  or or_5 (ALUsrc, demultiplexer_1_out0, call, demultiplexer_1_out15, demultiplexer_1_out8, demultiplexer_1_out9, demultiplexer_1_out10, rtn, reboot, halt);
  or or_6 (RegWrite, demultiplexer_1_out14, demultiplexer_1_out0, demultiplexer_1_out1, demultiplexer_1_out2, demultiplexer_1_out3, demultiplexer_1_out4, MemRead, demultiplexer_1_out7, demultiplexer_1_out8, demultiplexer_1_out9, demultiplexer_1_out10, demultiplexer_1_out12, demultiplexer_1_out13);
  or or_7 (typeI, demultiplexer_1_out8, demultiplexer_1_out9, demultiplexer_1_out10);
  or or_8 (or_8_out, demultiplexer_1_out7, halt);
  or or_9 (or_9_out, halt, reboot, rtn, demultiplexer_1_out15, demultiplexer_1_out0, MemWrite, demultiplexer_1_out11, demultiplexer_1_out7, demultiplexer_1_out8, demultiplexer_1_out9, demultiplexer_1_out10, call, demultiplexer_1_out4);
  or or_10 (branch, demultiplexer_1_out15, call);
  or or_11 (or_11_out, demultiplexer_1_out9, demultiplexer_1_out2);
  not not_1 (RegDst, or_9_out);
  or or_12 (isALU, demultiplexer_1_out1, demultiplexer_1_out2, demultiplexer_1_out3, demultiplexer_1_out4, demultiplexer_1_out14, demultiplexer_1_out13, demultiplexer_1_out11, demultiplexer_1_out12);
  Priority_Encoder #(.select(4)) priority_encoder_1 (
    .in0(or_3_out), .in1(or_11_out), .in2(or_4_out), .in3(demultiplexer_1_out12),
    .in4(demultiplexer_1_out13), .in5(demultiplexer_1_out14), .in6(demultiplexer_1_out0), .in8(or_1_out),
    .in9(call), .in10(or_2_out), .in11(reboot), .in12(or_8_out), .in13(MemRead), .in15(demultiplexer_1_out4),
    .out(ALUOp));  // open: in7, in14, gs, en_out, en_in

  assign MemToReg = MemRead;
endmodule
